// Logisim project Ctl_Shift_Add_Sub_Mov.circ as structural Verilog: 5 circuits, main circuit table_de_verite
module Shift_Add_Sub_Mov (
  input  Enable,
  input  [15:0] Instruction,
  output [3:0] Flags_Update_Mask,
  output Carry,
  output Imm32_Enable,
  output [2:0] Rm,
  output [2:0] Rn,
  output [2:0] Rd,
  output [4:0] Imm5,
  output [31:0] Imm32,
  output [3:0] ALU_Opcode
);

  wire carry_table_1_carry, comparator_1_lt, im32_enable_table_1_im32;
  wire [3:0] flags_table_1_flags, table_de_verite_1_codop;
  wire [4:0] bitselector_3_out, bitselector_4_out, transistor_1_out;
  wire [5:0] bitselector_2_out;
  wire [8:0] bitselector_1_out;

  BitSelector #(.group(9), .width(16)) bitselector_1 (.in(Instruction), .out(bitselector_1_out), .sel(1'b1));
  BitSelector #(.group(6), .width(16)) bitselector_2 (.in(Instruction), .out(bitselector_2_out), .sel(2'b01));
  BitSelector #(.group(5), .width(9)) bitselector_3 (.in(bitselector_1_out), .out(bitselector_3_out), .sel(1'b0));
  BitSelector #(.group(5), .width(6)) bitselector_4 (.in(bitselector_2_out), .out(bitselector_4_out), .sel(1'b0));
  Comparator #(.width(5)) comparator_1 (.a(bitselector_3_out), .b(5'b01100), .lt(comparator_1_lt));  // open: gt, eq
  Transistor #(.\type ("n"), .width(5)) transistor_1 (
    .in(bitselector_4_out), .out(transistor_1_out), .gate(comparator_1_lt));
  Multiplexer #(.enable("false"), .width(4)) multiplexer_1 (
    .in0(4'b0000), .in1(flags_table_1_flags), .out(Flags_Update_Mask), .sel(Enable));
  Flags_table flags_table_1 (.codop(bitselector_3_out), .flags(flags_table_1_flags));
  Multiplexer #(.enable("false")) multiplexer_2 (.in0(1'b0), .in1(carry_table_1_carry), .out(Carry), .sel(Enable));
  carry_table carry_table_1 (.codop(bitselector_3_out), .carry(carry_table_1_carry));
  Multiplexer #(.enable("false")) multiplexer_3 (
    .in0(1'b0), .in1(im32_enable_table_1_im32), .out(Imm32_Enable), .sel(Enable));
  Im32_Enable_table im32_enable_table_1 (.codop(bitselector_3_out), .im32(im32_enable_table_1_im32));
  Multiplexer #(.enable("false"), .width(3)) multiplexer_4 (.in0(3'b000), .out(Rm), .sel(Enable));  // open: in1
  Multiplexer #(.enable("false"), .width(3)) multiplexer_5 (.in0(3'b000), .out(Rn), .sel(Enable));  // open: in1
  Multiplexer #(.enable("false"), .width(3)) multiplexer_6 (.in0(3'b000), .out(Rd), .sel(Enable));  // open: in1
  Multiplexer #(.enable("false"), .width(5)) multiplexer_7 (
    .in0({5{1'b0}}), .in1(transistor_1_out), .out(Imm5), .sel(Enable));
  Multiplexer #(.enable("false"), .width(32)) multiplexer_8 (.in0({32{1'b0}}), .out(Imm32), .sel(Enable));  // open: in1
  Multiplexer #(.enable("false"), .width(4)) multiplexer_9 (
    .in0(4'b0000), .in1(table_de_verite_1_codop), .out(ALU_Opcode), .sel(Enable));
  table_de_verite table_de_verite_1 (.opcode(bitselector_3_out), .codop(table_de_verite_1_codop));

  // Other names for the same wires on the sheet: E = Enable

  // Notes on the sheet:
  //   Note: ALU uses Rn register for shifts. Use Rn instead of Rm for shifts (immediate) here too
  //   Note 3: Imm32_Enable forces the use of the immediate for Rm register
  //   Note 2: MOV uses RSB ALU opcode with Imm8 reversed so that it is copied to output register
  //   Pull output low on Enable = 0
  //   Enable carry for SUB since it is reversed in ALU
  //   ALU will use Imm32 instead of Rm
  //   only ADD and SUB use Rm
endmodule

module table_de_verite (
  input  [4:0] opcode,
  output [3:0] codop
);

  wire not_1_out;

  not not_1 (not_1_out, opcode[4]);
  not not_2 (codop[1], opcode[3]);
  and and_1 (codop[0], not_1_out, opcode[2]);

  assign codop[3:2] = opcode[4:3];
endmodule

module carry_table (
  input  [4:0] codop,
  output carry
);

  wire and_1_out, not_1_out, not_2_out, not_3_out;

  not not_1 (not_1_out, codop[3]);
  not not_2 (not_2_out, codop[2]);
  not not_3 (not_3_out, codop[1]);
  and and_1 (and_1_out, not_1_out, not_3_out);
  or or_1 (carry, and_1_out, not_2_out, codop[0], codop[4]);
endmodule

module Im32_Enable_table (
  input  [4:0] codop,
  output im32
);

  wire not_1_out;

  not not_1 (not_1_out, codop[4]);
  and and_1 (im32, not_1_out, codop[2]);
endmodule

module Flags_table (
  input  [4:0] codop,
  output [3:0] flags
);

  wire and_1_out, and_2_out, and_3_out, not_1_out;

  not not_1 (not_1_out, codop[4]);
  or or_1 (flags[1], not_1_out, codop[2], codop[3]);
  and and_1 (and_1_out, codop[3], codop[2]);
  and and_2 (and_2_out, codop[4], codop[2]);
  and and_3 (and_3_out, codop[4], codop[3]);
  or or_2 (flags[0], and_1_out, and_2_out, and_3_out);

  assign flags[3:2] = 2'b11;
endmodule
